# Fritzing sketch Schematics_without_change_machine (saved by Fritzing 0.9.3b)
breadboards: 1

parts:
  YF-S201_Flow_Meter1 = YF-S201 Water Flow Meter
  VALVE1 = Plastic Solenoid Valve
  U1 = 2-Channel 5v Relay Shield [package=relay-2ch5v10a]
  J1 = Power Jack [package=power_jack_pth]
  Composant1 = Arduino Nano (Rev3.0)

nets:
  N1: YF-S201_Flow_Meter1.SIG, Composant1.D2
  GND: YF-S201_Flow_Meter1.GND, U1.GND, Composant1.GND
  VCC: YF-S201_Flow_Meter1.VCC, U1.VCC, Composant1.5V
  N2: VALVE1.no_name_yet#1, U1.K1-On
  N3: VALVE1.no_name_yet#2, J1.GND
  N4: U1.IN1, Composant1.D4
  N5: U1.K1-In, J1.GNDBREAK
  N6: U1.K2-Off, U1.K2-On

notes:
  WATER ->
  12V

custom parts:
  YF-S201 Water Flow Meter: The YF-S201 Flow Meter. The input voltage is 5V to 24V (DC).
  2-Channel 5v Relay Shield: 2 Channel 5v Relay Shield w. 2x SPD-06VDC-SD-C
